# Fritzing sketch 001-led (saved by Fritzing 0.9.6b)
breadboards: 1

parts:
  Part1 = Arduino Mega 2560 (Rev3)
  LED1 = LED - 5mm [color="Red (633nm)" current=0.030 package="5 mm [THT]"]
  R1 = Resistor [tolerance=±5% power=0.25 resistance=220 package=THT]

nets:
  N1: Part1.GND, LED1.cathode
  N2: Part1.D2_PWM, R1.Pin_0
  N3: LED1.anode, R1.Pin_1
