# Fritzing sketch 003-simple-arduino-circuit-resistor-in-series (saved by Fritzing 0.9.6b)
breadboards: 1

parts:
  Part1 = Arduino Uno (Rev3)
  R1 = Resistor [tolerance=±5% power=0.25 resistance=220 package=THT]
  LED1 = LED - 5mm [color="Red (633nm)" current=0.030 package="5 mm [THT]"]
  R2 = Resistor [tolerance=±5% power=0.25 resistance=220 package=THT]

nets:
  N1: Part1.5V, R2.Pin_0
  N2: Part1.GND, LED1.cathode
  N3: R1.Pin_0, R2.Pin_1
  N4: R1.Pin_1, LED1.anode
