# Fritzing sketch arduino-serial-communication-1 (saved by Fritzing 0.9.6b)

parts:
  Part1 = Arduino Mega 2560 (Rev3)
  Part2 = Arduino Mega 2560 (Rev3)

nets:
  N1: Part1.D11_PWM, Part2.D10_PWM
  GND: Part1.GND, Part2.GND
