# Fritzing sketch arduino-serial-communication-2 (saved by Fritzing 0.9.6b)

parts:
  Part1 = Arduino Mega 2560 (Rev3)
  Part2 = Arduino Mega 2560 (Rev3)
  Mod1 = KY-008 Laser Transmitter Module [package="Breakout board"]
  R1 = PHOTOCELL [package=photocell-kit]
  R2 = Rotary Potentiometer (Small) [maximum_resistance=100kΩ package=THT]

nets:
  N1: Part1.D11_PWM, Mod1.S
  N2: Part1.GND, Mod1.-
  N3: Part2.D10_PWM, R1.P$2, R2.leg1
  N4: Part2.5V, R1.P$1
  N5: Part2.GND, R2.wiper

notes:
  ↓

custom parts:
  KY-008 Laser Transmitter Module: KY-008 Laser Transmitter Module, emits a dot shaped red laser beam.
