# Fritzing sketch lcd-00 (saved by Fritzing 0.9.6b)
breadboards: 1

parts:
  LCD1 = LCD screen
  Part1 = Arduino Mega 2560 (Rev3)
  LCM1602_IIC2 = LCM1602 IIC [part_number="LCM1602 IIC" chip_label="LCM1602 IIC" package="DIP (Dual Inline) [THT]"]

nets:
  VSS: LCD1.VSS, LCM1602_IIC2.VSS
  VDD: LCD1.VDD, LCM1602_IIC2.VDD
  N1: LCD1.V0, LCM1602_IIC2.V0
  N2: LCD1.RS, LCM1602_IIC2.RS
  N3: LCD1.R/W, LCM1602_IIC2.RW
  N4: LCD1.E, LCM1602_IIC2.E
  N5: LCD1.DB0, LCM1602_IIC2.D0
  N6: LCD1.DB1, LCM1602_IIC2.D1
  N7: LCD1.DB2, LCM1602_IIC2.D2
  N8: LCD1.DB3, LCM1602_IIC2.D3
  N9: LCD1.DB4, LCM1602_IIC2.D4
  N10: LCD1.DB5, LCM1602_IIC2.D5
  N11: LCD1.DB6, LCM1602_IIC2.D6
  N12: LCD1.DB7, LCM1602_IIC2.D7
  N13: LCD1.LED+, LCM1602_IIC2.A
  N14: LCD1.LED-, LCM1602_IIC2.K
  N15: Part1.D21/SCL, LCM1602_IIC2.SCL
  N16: Part1.D20/SDA, LCM1602_IIC2.SDA
  5V: Part1.5V, LCM1602_IIC2.VCC
  GND: Part1.GND, LCM1602_IIC2.GND

custom parts:
  LCM1602 IIC: I2C-Module to use a 1602 or 2004 LCD on with the wire.h libory Serial LCD Modul
